// Logisim project simulace.circ as structural Verilog: 3 circuits, main circuit main
module main (
);

  wire clock_1_out, cnt_1_x, cnt_1_y, cnt_1_z, dek_1_a, dek_1_b, dek_1_c, dek_1_d;

  CNT cnt_1 (.Z(cnt_1_z), .Y(cnt_1_y), .X(cnt_1_x), .SCK(clock_1_out));
  Clock clock_1 (.out(clock_1_out));
  // Probe on nothing
  DEK dek_1 (.Z(cnt_1_z), .Y(cnt_1_y), .X(cnt_1_x), .B(dek_1_b), .C(dek_1_c), .D(dek_1_d), .A(dek_1_a));
  LED led_1 (.in(dek_1_c));
  LED led_2 (.in(dek_1_a));
  LED led_3 (.in(dek_1_d));
  LED led_4 (.in(dek_1_b));
  LED led_5 (.in(dek_1_b));
  LED led_6 (.in(dek_1_d));
  LED led_7 (.in(dek_1_c));
endmodule

module CNT (
  input  SCK,
  output Z,
  output Y,
  output X
);

  wire and_1_out, d_ff_1_qn, d_ff_2_qn, d_ff_3_qn;

  D_Flip_Flop d_ff_1 (.clk(SCK), .D(d_ff_1_qn), .Q(Z), .Qn(d_ff_1_qn));  // open: preset, en, reset
  D_Flip_Flop d_ff_2 (.clk(d_ff_1_qn), .D(d_ff_2_qn), .Q(Y), .Qn(d_ff_2_qn), .reset(and_1_out));  // open: preset, en
  D_Flip_Flop d_ff_3 (.clk(d_ff_2_qn), .D(d_ff_3_qn), .Q(X), .Qn(d_ff_3_qn), .reset(and_1_out));  // open: preset, en
  and and_1 (and_1_out, Y, Z, X);
endmodule

module DEK (
  input  Z,
  input  Y,
  input  X,
  output A,
  output B,
  output D,
  output C
);

  wire not_1_out;

  not not_1 (not_1_out, Z);
  and and_1 (D, Y, X);
  or or_1 (B, not_1_out, X, Y);

  assign A = Z;
  assign C = X;
endmodule
